# Fritzing sketch SIDPod (saved by Fritzing 0.9.10b)
breadboards: 1

parts:
  Pico_H1 = Raspberry Pi Pico H
  Part1 = Adafruit MAX98357A I2S 3W Class D Amplifier [part_number="Adafruit #3006"]
  Part2 = TRRS 3.5mm Jack Breakout  # not connected
  ENCODER1 = Rotary Encoder with Knob
  Part3 = OLED Monochrome 128x32 I2C [part_number=931]
  R1 = Resistor [tolerance=±5% power=0.25 resistance=100 package=THT]
  R2 = Resistor [tolerance=±5% power=0.25 resistance=100 package=THT]
  U1 = LIPO-1000mAh [package=lipo-1000]

nets:
  N1: Pico_H1.VSYS, Part1.VIN, U1.+
  GND: Pico_H1.GND, Part1.GND, ENCODER1.no_name_yet#5, Part3.GND, U1.-
  3V3: Pico_H1.3V3, Part3.VIN
  N2: Pico_H1.GP28_A2, Part1.LRCLK
  N3: Pico_H1.GP27_A1, Part1.BCLK
  N4: Pico_H1.GP26_A0, Part1.DIN
  N5: Pico_H1.GP15, Part1.SD_MODE
  N6: Pico_H1.GP12, ENCODER1.no_name_yet#4
  N7: Pico_H1.GP11, ENCODER1.no_name_yet#1
  N8: Pico_H1.GP10, ENCODER1.no_name_yet#3
  N9: Pico_H1.GP3, Part3.SCL
  N10: Pico_H1.GP2, Part3.SDA
  N11: Part1.VO-, R1.Pin_1
  N12: Part1.VO+, R2.Pin_1

custom parts:
  Raspberry Pi Pico H: Raspberry Pi Pico H. Based around the RP2040 microcontroller the Pico H is a low cost microcontroller device bringing Raspberry Pi quality, cost, and easy of use to the microcontroller space.
  Adafruit MAX98357A I2S 3W Class D Amplifier: Listen to this good news - we now have an all in one digital audio amp breakout board that works incredibly well with the Raspberry Pi! If you're looking for an easy and low cost way to get you digital sound files bumpin' then the MAX08357 I2S Amp Breakout is for you. It takes standard I2S digital audio input and, not only decodes it into analog, but also amplifies it directly into a speaker.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
  Rotary Encoder with Knob: Rotary Encoder with 1/4" Shaft and Knob
  OLED Monochrome 128x32 I2C: These displays are small, only about 1" diagonal, but very readable due to the high contrast of an OLED display. This display is made of 128x32 individual white OLED pixels, each one is turned on or off by the controller chip. Because the display makes its own light, no backlight is required. This reduces the power required to run the OLED and is why the display has such high contrast; we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
